# Fritzing sketch circuito-vibranota (saved by Fritzing 0.9.3b)
breadboards: 1

parts:
  Componente3 = Arduino Micro (Rev3)
  R2 = Resistor [tolerance=±5% resistance=2.2k package=THT]
  S1 = Pushbutton [package="[THT]"]
  S2 = Pushbutton [package="[THT]"]
  R4 = Resistor [tolerance=±5% resistance=2.2k package=THT]
  R5 = Resistor [tolerance=±5% resistance=2.2k package=THT]
  S3 = Pushbutton [package="[THT]"]
  S4 = Pushbutton [package="[THT]"]
  R6 = Resistor [tolerance=±5% resistance=2.2k package=THT]
  S5 = Pushbutton [package="[THT]"]
  R7 = Resistor [tolerance=±5% resistance=2.2k package=THT]
  M1 = DC Motor
  S6 = Pushbutton [package="[THT]"]
  S7 = Pushbutton [package="[THT]"]
  R8 = Resistor [tolerance=±5% resistance=2.2k package=THT]
  R9 = Resistor [tolerance=±5% resistance=2.2k package=THT]
  J1 = Piezo Speaker

nets:
  N1: Componente3.GND, Componente3.D3/SCL, R2.Pin_1, R4.Pin_1, R5.Pin_1, R6.Pin_1, R7.Pin_1, M1.pin_2, R8.Pin_1, R9.Pin_1
  N2: Componente3.D2/SDA, S7.Pin_3, S7.Pin_4, R9.Pin_0
  N3: Componente3.D4_PWM/A6, S6.Pin_3, S6.Pin_4, R8.Pin_0
  N4: Componente3.D5_PWM, J1.pin2
  N5: Componente3.D6_PWM/A7, R2.Pin_0, S1.Pin_3, S1.Pin_4
  N6: Componente3.D7, S2.Pin_3, S2.Pin_4, R4.Pin_0
  N7: Componente3.D8_PWM/A8, R5.Pin_0, S3.Pin_3, S3.Pin_4
  N8: Componente3.D9_PWM/A9, S4.Pin_3, S4.Pin_4, R6.Pin_0
  N9: Componente3.D10_PWM/A10, S5.Pin_3, S5.Pin_4, R7.Pin_0
  N10: Componente3.3V3, S1.Pin_1, S1.Pin_2, S2.Pin_1, S2.Pin_2, S3.Pin_1, S3.Pin_2, S4.Pin_1, S4.Pin_2, S5.Pin_1, S5.Pin_2, S6.Pin_1, S6.Pin_2, S7.Pin_1, S7.Pin_2
  N11: M1.pin_1, J1.pin1

notes:
  Tecnólogo em Análise e Desenvolvimento de Sistemas - TADS
  Desenvolvido por Denis Lopes - denislopesmoura@gmail.com
  Instituto Federal de Educação de Pernambuco
